# Fritzing sketch design (saved by Fritzing 0.9.10b)
breadboards: 1

parts:
  Pico_H1 = Raspberry Pi Pico H
  HC-SR04_Sensor_1 = HC-SR04 Ultrasonic Distance Sensor
  M1 = gear-motor  # not connected
  M2 = gear-motor  # not connected
  L298N2 = L298N DC motor driver

nets:
  N1: Pico_H1.VBUS, HC-SR04_Sensor_1.VCC
  GND: Pico_H1.GND, HC-SR04_Sensor_1.GND
  N2: Pico_H1.GP15, L298N2.ENA
  N3: Pico_H1.GP14, L298N2.IN1
  N4: Pico_H1.GP13, L298N2.IN2
  N5: Pico_H1.GP12, L298N2.IN3
  N6: Pico_H1.GP11, L298N2.IN4
  N7: Pico_H1.GP10, L298N2.ENB

custom parts:
  Raspberry Pi Pico H: Raspberry Pi Pico H. Based around the RP2040 microcontroller the Pico H is a low cost microcontroller device bringing Raspberry Pi quality, cost, and easy of use to the microcontroller space.
  L298N DC motor driver: 2x DC motor driver with 78M05 positive voltage regulator (7..35 V) L298N: max 46 V, 2 A Set 5 V Enable jumper to enable 5 V regultor (needed for the L298N) and +5 V output at screw terminal or supply external +5 V at screw terminal Set ENA and/or ENB to +5 V to enable motor permanently or supply ENA and/or ENB with PWM signal IN1 and IN2 set rotation directory for motor A (OUT1/OUT2) IN2 and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
